// Logisim project monociclo_1.circ as structural Verilog: 1 circuit, main circuit main
module main (
  input  in_1,
  input  in_2
);

  wire and_1_out, CLK, controlunit_alt_1_p3, controlunit_alt_1_p4, controlunit_alt_1_p5,
       controlunit_alt_1_p6, controlunit_alt_1_p7, controlunit_alt_1_p8, controlunit_alt_1_p9,
       controlunit_alt_1_p10, controlunit_alt_1_p11, controlunit_alt_1_p12, controlunit_alt_1_p13,
       controlunit_alt_1_p14, controlunit_alt_1_p15, decoder_alt_1_p2, decoder_alt_1_p3, decoder_alt_1_p5,
       decoder_alt_1_p6, decoder_alt_1_p7, decoder_alt_1_p10, ula_1_p5, xor_1_out;
  wire [4:0] decoder_alt_1_p4, decoder_alt_1_p8, decoder_alt_1_p9, jumpaddress_1_p9, multiplexer_1_out;
  wire [31:0] adder_1_out, adder_2_out, bit_extender_1_out, immediatecomplement_1_p2, jumpaddress_1_p4,
       jumpaddress_1_p10, multiplexer_3_out, multiplexer_4_out, multiplexer_5_out, multiplexer_6_out,
       multiplexer_7_out, multiplexer_8_out, multiplexer_9_out, multiplexer_10_out, ram_1_dout, register_1_q,
       registerfile_1_p1, registerfile_1_p2, rom_1_data, shifter_1_out, ula_1_p4, undriven;

  Counter #(.max('hffff), .width(16)) counter_1 (.clk(CLK));  // open: clr, load, up, count, D, carry, Q
  Register #(.width(32)) register_1 (.D(multiplexer_8_out), .en(1'b1), .clk(CLK), .Q(register_1_q), .clr(in_1));
  Clock clock_1 (.out(CLK));
  ROM #(.addrWidth(10), .dataWidth(32)) rom_1 (.addr(register_1_q[11:2]), .data(rom_1_data));
  // decoder_alt decoder_alt_1: pin names not known; wires that end beside it: rom_1_data, decoder_alt_1_p2, decoder_alt_1_p3, decoder_alt_1_p4, decoder_alt_1_p5, decoder_alt_1_p6, decoder_alt_1_p7, decoder_alt_1_p8, decoder_alt_1_p9, decoder_alt_1_p10
  Adder #(.width(32)) adder_1 (.a(register_1_q), .b(32'h4), .out(adder_1_out));  // open: cin, cout
  // ControlUnit_alt controlunit_alt_1: pin names not known; wires that end beside it: decoder_alt_1_p2, decoder_alt_1_p3, controlunit_alt_1_p3, controlunit_alt_1_p4, controlunit_alt_1_p5, controlunit_alt_1_p6, controlunit_alt_1_p7, controlunit_alt_1_p8, controlunit_alt_1_p9, controlunit_alt_1_p10, controlunit_alt_1_p11, controlunit_alt_1_p12, controlunit_alt_1_p13, controlunit_alt_1_p14, controlunit_alt_1_p15
  Multiplexer #(.width(5)) multiplexer_1 (
    .in0(decoder_alt_1_p8), .in1(decoder_alt_1_p9), .out(multiplexer_1_out), .sel(decoder_alt_1_p10));
  assign bit_extender_1_out = {{27{1'b0}}, decoder_alt_1_p4};  // Bit_Extender bit_extender_1
  // immediateComplement immediatecomplement_1: pin names not known; wires that end beside it: decoder_alt_1_p5, immediatecomplement_1_p2
  // JumpAddress jumpaddress_1: pin names not known; wires that end beside it: controlunit_alt_1_p9, decoder_alt_1_p6, adder_1_out, jumpaddress_1_p4, CLK, controlunit_alt_1_p14, decoder_alt_1_p7, decoder_alt_1_p8, jumpaddress_1_p9, jumpaddress_1_p10, in_2
  Multiplexer #(.width(5)) multiplexer_2 (
    .in0(multiplexer_1_out), .in1({5{1'b1}}), .out(jumpaddress_1_p9), .sel(controlunit_alt_1_p15));
  Shifter #(.width(32)) shifter_1 (.in(immediatecomplement_1_p2), .\dist (5'b00010), .out(shifter_1_out));
  Adder #(.width(32)) adder_2 (.a(adder_1_out), .b(shifter_1_out), .out(adder_2_out));  // open: cin, cout
  // RegisterFile registerfile_1: pin names not known; wires that end beside it: registerfile_1_p1, registerfile_1_p2
  Multiplexer #(.width(32)) multiplexer_3 (
    .in0(adder_1_out), .in1(adder_2_out), .out(multiplexer_3_out), .sel(and_1_out));
  and and_1 (and_1_out, xor_1_out, controlunit_alt_1_p3);
  xor xor_1 (xor_1_out, ula_1_p5, controlunit_alt_1_p4);
  Multiplexer #(.width(32)) multiplexer_4 (
    .in0(registerfile_1_p1), .in1(registerfile_1_p2), .out(multiplexer_4_out), .sel(controlunit_alt_1_p7));
  Multiplexer #(.width(32)) multiplexer_5 (
    .in0(registerfile_1_p2), .in1(immediatecomplement_1_p2), .out(multiplexer_5_out),
    .sel(controlunit_alt_1_p8));
  Multiplexer #(.width(32)) multiplexer_6 (
    .in0(multiplexer_5_out), .in1(bit_extender_1_out), .out(multiplexer_6_out), .sel(controlunit_alt_1_p7));
  Multiplexer #(.width(32)) multiplexer_7 (
    .in0(multiplexer_3_out), .in1(jumpaddress_1_p4), .out(multiplexer_7_out), .sel(controlunit_alt_1_p5));
  Multiplexer #(.width(32)) multiplexer_8 (
    .in0(multiplexer_7_out), .in1(registerfile_1_p1), .out(multiplexer_8_out), .sel(controlunit_alt_1_p6));
  // ULA ula_1: pin names not known; wires that end beside it: multiplexer_4_out, multiplexer_6_out, controlunit_alt_1_p13, ula_1_p4, ula_1_p5
  RAM #(.addrWidth(10), .dataWidth(32), .enables("line")) ram_1 (
    .addr(ula_1_p4[11:2]), .we(controlunit_alt_1_p11), .clk(CLK), .din(registerfile_1_p2), .dout(ram_1_dout));
  // NoConnect on undriven
  Multiplexer #(.width(32)) multiplexer_9 (
    .in0(undriven), .in1(ram_1_dout), .out(multiplexer_9_out), .sel(controlunit_alt_1_p12));
  Multiplexer #(.width(32)) multiplexer_10 (
    .in0(ula_1_p4), .in1(multiplexer_9_out), .out(multiplexer_10_out), .sel(controlunit_alt_1_p10));
  Multiplexer #(.width(32)) multiplexer_11 (
    .in0(multiplexer_10_out), .in1(adder_1_out), .out(jumpaddress_1_p10), .sel(controlunit_alt_1_p15));

  // Notes on the sheet:
  //   contents of rom_1 (hex, n*v repeats v):
  //   20080000 2009000a 200a0000 214b0001 ad0b0000 21080004 214a0001 1549fffb 20080000 200a0000 20100000
  //   11490005 8d0b0000 20b8020 21080004 214a0001 800000b ac100028 8c0c0028 8000013
endmodule
