// Logisim project pipeline_2_v2_bubble.circ as structural Verilog: 1 circuit, main circuit main
module main (
  input  Clear_Pipeline,
  input  Clear_Memory,
  input  in_3,
  input  in_4
);

  wire and_1_out, branchhandlerv2_1_p4, branchhandlerv2_1_p5, CLK, controlunit_1_p3, controlunit_1_p4,
       controlunit_1_p5, controlunit_1_p6, controlunit_1_p7, controlunit_1_p8, controlunit_1_p9,
       controlunit_1_p10, controlunit_1_p11, controlunit_1_p12, controlunit_1_p13, controlunit_1_p14,
       controlunit_1_p15, controlunit_1_p16, controlunit_1_p17, decoder_alt_1_p4, decoder_alt_1_p5,
       decoder_alt_1_p7, decoder_alt_1_p8, decoder_alt_1_p9, ex_memv2_1_p8, ex_memv2_1_p9, ex_memv2_1_p10,
       ex_memv2_1_p11, hazard_detection_unit_1_p6, hazard_detection_unit_1_p7, hazard_detection_unit_1_p8,
       hazard_detection_unit_1_p9, hazard_detection_unit_1_p10, hazard_detection_unit_1_p11,
       hazard_detection_unit_1_p12, hazard_detection_unit_1_p24, id_exv2_1_p11, id_exv2_1_p12, id_exv2_1_p13,
       id_exv2_1_p14, id_exv2_1_p15, id_exv2_1_p16, id_exv2_1_p17, if_id_1_p2, immediatecomplement_1_p2,
       mem_wb_1_p6, mem_wb_1_p7, mem_wb_1_p8, nor_1_out, not_1_out, not_2_out, not_3_out, or_1_out, or_2_out,
       or_3_out, or_5_out, or_6_out, ula_1_p4, ula_1_p12, xor_1_out;
  wire [4:0] decoder_alt_1_p6, decoder_alt_1_p10, decoder_alt_1_p11, multiplexer_2_out, multiplexer_3_out;
  wire [31:0] adder_1_out, adder_2_out, bit_extender_1_out, hazard_detection_unit_1_p19,
       hazard_detection_unit_1_p20, hazard_detection_unit_1_p21, hazard_detection_unit_1_p22,
       immediatecomplement_1_p3, jumpaddress_1_p2, jumpaddress_1_p3, mem_wb_1_p9, multiplexer_1_out,
       multiplexer_4_out, multiplexer_5_out, multiplexer_6_out, multiplexer_7_out, multiplexer_8_out,
       multiplexer_9_out, multiplexer_10_out, multiplexer_11_out, ram_1_dout, register_1_q,
       registerfile_1_p1, registerfile_1_p2, rom_1_data, shifter_1_out, ula_1_p9, ula_1_p10, undriven,
       undriven_2, xor_2_out;

  Multiplexer #(.width(32)) multiplexer_1 (
    .in0(adder_1_out), .in1(multiplexer_6_out), .out(multiplexer_1_out), .sel(branchhandlerv2_1_p4));
  Register #(.width(32)) register_1 (.D(multiplexer_1_out), .en(not_1_out), .clk(CLK), .Q(register_1_q), .clr(in_4));
  not not_1 (not_1_out, hazard_detection_unit_1_p10);
  Counter #(.max('hffff), .width(16)) counter_1 (.clk(CLK));  // open: clr, load, up, count, D, carry, Q
  Clock clock_1 (.out(CLK));
  Adder #(.width(32)) adder_1 (.a(register_1_q), .b(32'h4), .out(adder_1_out));  // open: cin, cout
  ROM #(.addrWidth(10), .dataWidth(32)) rom_1 (.addr(register_1_q[11:2]), .data(rom_1_data));
  not not_2 (not_2_out, hazard_detection_unit_1_p11);
  // IF_ID if_id_1: pin names not known; wires that end beside it: CLK, if_id_1_p2
  or or_1 (or_1_out, Clear_Pipeline, branchhandlerv2_1_p5);
  // decoder_alt decoder_alt_1: pin names not known; wires that end beside it: adder_1_out, rom_1_data, if_id_1_p2, decoder_alt_1_p4, decoder_alt_1_p5, decoder_alt_1_p6, decoder_alt_1_p7, decoder_alt_1_p8, decoder_alt_1_p9, decoder_alt_1_p10, decoder_alt_1_p11
  or or_2 (or_2_out, controlunit_1_p9, controlunit_1_p10, controlunit_1_p11);
  // immediateComplement immediatecomplement_1: pin names not known; wires that end beside it: decoder_alt_1_p7, immediatecomplement_1_p2, immediatecomplement_1_p3
  assign bit_extender_1_out = {{27{1'b0}}, decoder_alt_1_p6};  // Bit_Extender bit_extender_1
  // ControlUnit controlunit_1: pin names not known; wires that end beside it: decoder_alt_1_p4, decoder_alt_1_p5, controlunit_1_p3, controlunit_1_p4, controlunit_1_p5, controlunit_1_p6, controlunit_1_p7, controlunit_1_p8, controlunit_1_p9, controlunit_1_p10, controlunit_1_p11, controlunit_1_p12, controlunit_1_p13, controlunit_1_p14, controlunit_1_p15, controlunit_1_p16, controlunit_1_p17, immediatecomplement_1_p2
  Multiplexer #(.width(5)) multiplexer_2 (
    .in0(decoder_alt_1_p10), .in1(decoder_alt_1_p11), .out(multiplexer_2_out), .sel(controlunit_1_p17));
  Multiplexer #(.width(5)) multiplexer_3 (
    .in0(multiplexer_2_out), .in1({5{1'b1}}), .out(multiplexer_3_out), .sel(controlunit_1_p6));
  // JumpAddress jumpaddress_1: pin names not known; wires that end beside it: decoder_alt_1_p8, jumpaddress_1_p2, jumpaddress_1_p3
  // BranchHandlerv2 branchhandlerv2_1: pin names not known; wires that end beside it: or_2_out, CLK, Clear_Pipeline, branchhandlerv2_1_p4, branchhandlerv2_1_p5
  not not_3 (not_3_out, CLK);
  Shifter #(.width(32)) shifter_1 (.in(immediatecomplement_1_p3), .\dist (5'b00010), .out(shifter_1_out));
  Adder #(.width(32)) adder_2 (.a(jumpaddress_1_p2), .b(shifter_1_out), .out(adder_2_out));  // open: cin, cout
  or or_3 (or_3_out, xor_2_out[31], xor_2_out[30], xor_2_out[29], xor_2_out[28], xor_2_out[27], xor_2_out[26], xor_2_out[25], xor_2_out[24], xor_2_out[23], xor_2_out[22], xor_2_out[21], xor_2_out[20], xor_2_out[19], xor_2_out[18], xor_2_out[17], xor_2_out[16]);
  and and_1 (and_1_out, controlunit_1_p9, xor_1_out);
  xor xor_1 (xor_1_out, nor_1_out, controlunit_1_p8);
  Multiplexer #(.width(32)) multiplexer_4 (
    .in0(jumpaddress_1_p2), .in1(adder_2_out), .out(multiplexer_4_out), .sel(and_1_out));
  Multiplexer #(.width(32)) multiplexer_5 (
    .in0(multiplexer_4_out), .in1(jumpaddress_1_p3), .out(multiplexer_5_out), .sel(controlunit_1_p10));
  // RegisterFile registerfile_1: pin names not known; wires that end beside it: registerfile_1_p1, registerfile_1_p2
  nor nor_1 (nor_1_out, or_3_out, or_5_out);
  or or_4 (branchhandlerv2_1_p4, and_1_out, controlunit_1_p11, controlunit_1_p10);
  Multiplexer #(.width(32)) multiplexer_6 (
    .in0(multiplexer_5_out), .in1(registerfile_1_p1), .out(multiplexer_6_out), .sel(controlunit_1_p11));
  assign xor_2_out = registerfile_1_p1 ^ registerfile_1_p2;  // XOR_Gate xor_2, 32 bits wide
  or or_5 (or_5_out, xor_2_out[15], xor_2_out[14], xor_2_out[13], xor_2_out[12], xor_2_out[11], xor_2_out[10], xor_2_out[9], xor_2_out[8], xor_2_out[7], xor_2_out[6], xor_2_out[5], xor_2_out[4], xor_2_out[3], xor_2_out[2], xor_2_out[1], xor_2_out[0]);
  // Hazard_Detection_Unit hazard_detection_unit_1: pin names not known; wires that end beside it: CLK, controlunit_1_p4, controlunit_1_p3, decoder_alt_1_p9, decoder_alt_1_p10, hazard_detection_unit_1_p6, hazard_detection_unit_1_p7, hazard_detection_unit_1_p8, hazard_detection_unit_1_p9, hazard_detection_unit_1_p10, hazard_detection_unit_1_p11, hazard_detection_unit_1_p12, registerfile_1_p1, registerfile_1_p2, immediatecomplement_1_p3, bit_extender_1_out, multiplexer_3_out, jumpaddress_1_p2, hazard_detection_unit_1_p19, hazard_detection_unit_1_p20, hazard_detection_unit_1_p21, hazard_detection_unit_1_p22, hazard_detection_unit_1_p7, hazard_detection_unit_1_p24
  // ID_EXv2 id_exv2_1: pin names not known; wires that end beside it: controlunit_1_p5, controlunit_1_p6, controlunit_1_p7, controlunit_1_p12, controlunit_1_p13, controlunit_1_p14, controlunit_1_p15, controlunit_1_p16, CLK, hazard_detection_unit_1_p9, id_exv2_1_p11, id_exv2_1_p12, id_exv2_1_p13, id_exv2_1_p14, id_exv2_1_p15, id_exv2_1_p16, id_exv2_1_p17
  or or_6 (or_6_out, hazard_detection_unit_1_p12, Clear_Pipeline);
  Multiplexer #(.width(32)) multiplexer_7 (
    .in0(hazard_detection_unit_1_p20), .in1(hazard_detection_unit_1_p21), .out(multiplexer_7_out),
    .sel(id_exv2_1_p17));
  Multiplexer #(.width(32)) multiplexer_8 (
    .in0(hazard_detection_unit_1_p19), .in1(hazard_detection_unit_1_p20), .out(multiplexer_8_out),
    .sel(id_exv2_1_p16));
  Multiplexer #(.width(32)) multiplexer_9 (
    .in0(multiplexer_7_out), .in1(hazard_detection_unit_1_p22), .out(multiplexer_9_out), .sel(id_exv2_1_p16));
  // ULA ula_1: pin names not known; wires that end beside it: multiplexer_8_out, multiplexer_9_out, id_exv2_1_p15, ula_1_p4, ula_1_p4, hazard_detection_unit_1_p20, hazard_detection_unit_1_p7, hazard_detection_unit_1_p24, ula_1_p9, ula_1_p10, hazard_detection_unit_1_p6, ula_1_p12
  // EX_MEMv2 ex_memv2_1: pin names not known; wires that end beside it: hazard_detection_unit_1_p9, id_exv2_1_p11, id_exv2_1_p12, id_exv2_1_p13, id_exv2_1_p14, CLK, hazard_detection_unit_1_p8, ex_memv2_1_p8, ex_memv2_1_p9, ex_memv2_1_p10, ex_memv2_1_p11
  RAM #(.addrWidth(10), .asyncread("true"), .clearpin("true"), .dataWidth(32)) ram_1 (
    .addr(ula_1_p9[11:2]), .we(ex_memv2_1_p10), .oe(ex_memv2_1_p11), .clk(CLK), .din(ula_1_p10),
    .dout(ram_1_dout), .clr(Clear_Memory));
  // MEM_WB mem_wb_1: pin names not known; wires that end beside it: hazard_detection_unit_1_p8, ex_memv2_1_p8, ex_memv2_1_p9, ula_1_p9, CLK, mem_wb_1_p6, mem_wb_1_p7, mem_wb_1_p8, mem_wb_1_p9
  Multiplexer #(.width(32)) multiplexer_10 (
    .in0(mem_wb_1_p9), .in1(undriven), .out(multiplexer_10_out), .sel(mem_wb_1_p8));
  Multiplexer #(.width(32)) multiplexer_11 (
    .in0(multiplexer_10_out), .in1(undriven_2), .out(multiplexer_11_out), .sel(mem_wb_1_p7));

  // Other names for the same wires on the sheet: Clear = Clear_Pipeline

  // Notes on the sheet:
  //   Clear PC
  //   contents of rom_1 (hex, n*v repeats v):
  //   20080000 2009000a 200a0000 214b0001 ad0b0000 21080004 214a0001 1549fffb 20080000 200a0000 20100000
  //   11490005 8d0b0000 20b8020 21080004 214a0001 800000b ac100028 8c0c0028 8000013
endmodule
