// Logisim project pipeline_2_v2_fw_JTB.circ as structural Verilog: 4 circuits, main circuit main
module main (
  input  Clear_Pipeline,
  input  Clear_Memory,
  input  in_3,
  input  in_4,
  input  Clear
);

  wire and_1_out, and_2_out, branchhandlerv2_1_p4, branchhandlerv2_1_p5, CLK, comparator_1_eq,
       controlunit_1_p3, controlunit_1_p4, controlunit_1_p5, controlunit_1_p6, controlunit_1_p7,
       controlunit_1_p8, controlunit_1_p9, controlunit_1_p10, controlunit_1_p11, controlunit_1_p12,
       controlunit_1_p13, controlunit_1_p14, controlunit_1_p15, controlunit_1_p16, controlunit_1_p17,
       decoder_alt_1_p4, decoder_alt_1_p5, decoder_alt_1_p7, decoder_alt_1_p8, decoder_alt_1_p9,
       ex_memv2_1_p8, ex_memv2_1_p9, ex_memv2_1_p10, ex_memv2_1_p11, forwarding_unit_1_p5,
       forwarding_unit_1_p6, forwarding_unit_1_p7, forwarding_unit_1_p8, forwarding_unit_1_p20,
       id_exv2_1_p11, id_exv2_1_p12, id_exv2_1_p13, id_exv2_1_p15, id_exv2_1_p16, id_exv2_1_p17,
       if_id_jtb_1_p2, immediatecomplement_1_p2, jtb_1_p7, jtb_1_p9, jtb_1_p10, lw_hazard_handler_1_p2,
       lw_hazard_handler_1_p3, lw_hazard_handler_1_p4, lw_hazard_handler_1_p5, lw_hazard_handler_1_p6,
       mem_wb_1_p6, mem_wb_1_p7, mem_wb_1_p8, not_1_out, not_2_out, not_3_out, not_4_out, or_1_out, or_2_out,
       or_4_out, ula_1_p12, xor_1_out;
  wire [1:0] forwarding_unit_1_p9, forwarding_unit_1_p10;
  wire [4:0] decoder_alt_1_p6, decoder_alt_1_p10, decoder_alt_1_p11, multiplexer_5_out, multiplexer_6_out;
  wire [31:0] adder_1_out, adder_2_out, adder_3_out, bit_extender_1_out, forwarding_unit_1_p12,
       forwarding_unit_1_p17, forwarding_unit_1_p18, immediatecomplement_1_p3, jtb_1_p4, jtb_1_p6, jtb_1_p8,
       mem_wb_1_p9, multiplexer_1_out, multiplexer_2_out, multiplexer_3_out, multiplexer_4_out,
       multiplexer_7_out, multiplexer_8_out, multiplexer_9_out, multiplexer_10_out, multiplexer_12_out,
       multiplexer_13_out, multiplexer_14_out, multiplexer_15_out, multiplexer_16_out, multiplexer_17_out,
       ram_1_dout, register_1_q, registerfile_1_p1, registerfile_1_p2, shifter_1_out, TPCPlus4EX, ula_1_p4,
       ula_1_p6, ula_1_p9, ula_1_p10, undriven, undriven_2, undriven_3;

  Counter #(.max('hffff), .width(16)) counter_1 (.clk(CLK));  // open: clr, load, up, count, D, carry, Q
  Adder #(.width(32)) adder_1 (.a(register_1_q), .b(32'h4), .out(adder_1_out));  // open: cin, cout
  // jtb jtb_1: pin names not known; wires that end beside it: Clear, CLK, adder_1_out, jtb_1_p4, TPCPlus4EX, jtb_1_p6, jtb_1_p7, jtb_1_p8, jtb_1_p9, jtb_1_p10
  Multiplexer #(.width(32)) multiplexer_1 (
    .in0(multiplexer_3_out), .in1(multiplexer_9_out), .out(multiplexer_1_out), .sel(branchhandlerv2_1_p4));
  Register #(.width(32)) register_1 (.D(multiplexer_2_out), .en(not_1_out), .clk(CLK), .Q(register_1_q), .clr(in_4));
  not not_1 (not_1_out, lw_hazard_handler_1_p4);
  Multiplexer #(.width(32)) multiplexer_2 (
    .in0(multiplexer_1_out), .in1(multiplexer_3_out), .out(multiplexer_2_out), .sel(jtb_1_p9));
  Multiplexer #(.width(32)) multiplexer_3 (
    .in0(adder_1_out), .in1(adder_2_out), .out(multiplexer_3_out), .sel(jtb_1_p9));
  Adder #(.width(32)) adder_2 (.a(jtb_1_p8), .b(32'h4), .out(adder_2_out));  // open: cin, cout
  Multiplexer #(.width(32)) multiplexer_4 (.in0(register_1_q), .in1(jtb_1_p8), .out(multiplexer_4_out), .sel(jtb_1_p9));
  ROM #(.addrWidth(10), .dataWidth(32)) rom_1 (.addr(multiplexer_4_out[11:2]), .data(jtb_1_p4));
  Clock clock_1 (.out(CLK));
  not not_2 (not_2_out, lw_hazard_handler_1_p5);
  // IF_ID_JTB if_id_jtb_1: pin names not known; wires that end beside it: CLK, if_id_jtb_1_p2
  or or_1 (or_1_out, Clear_Pipeline, branchhandlerv2_1_p5);
  // Probe on if_id_jtb_1_p2
  // decoder_alt decoder_alt_1: pin names not known; wires that end beside it: multiplexer_3_out, jtb_1_p4, if_id_jtb_1_p2, decoder_alt_1_p4, decoder_alt_1_p5, decoder_alt_1_p6, decoder_alt_1_p7, decoder_alt_1_p8, decoder_alt_1_p9, decoder_alt_1_p10, decoder_alt_1_p11
  not not_3 (not_3_out, lw_hazard_handler_1_p4);
  or or_2 (or_2_out, controlunit_1_p9, controlunit_1_p10, controlunit_1_p11);
  // immediateComplement immediatecomplement_1: pin names not known; wires that end beside it: decoder_alt_1_p7, immediatecomplement_1_p2, immediatecomplement_1_p3
  assign bit_extender_1_out = {{27{1'b0}}, decoder_alt_1_p6};  // Bit_Extender bit_extender_1
  and and_1 (and_1_out, not_3_out, or_2_out);
  // ControlUnit controlunit_1: pin names not known; wires that end beside it: decoder_alt_1_p4, decoder_alt_1_p5, controlunit_1_p3, controlunit_1_p4, controlunit_1_p5, controlunit_1_p6, controlunit_1_p7, controlunit_1_p8, controlunit_1_p9, controlunit_1_p10, controlunit_1_p11, controlunit_1_p12, controlunit_1_p13, controlunit_1_p14, controlunit_1_p15, controlunit_1_p16, controlunit_1_p17, immediatecomplement_1_p2
  Multiplexer #(.width(5)) multiplexer_5 (
    .in0(decoder_alt_1_p10), .in1(decoder_alt_1_p11), .out(multiplexer_5_out), .sel(controlunit_1_p17));
  // JumpAddress jumpaddress_1: pin names not known; wires that end beside it: decoder_alt_1_p8, TPCPlus4EX, jtb_1_p6
  // BranchHandlerv2 branchhandlerv2_1: pin names not known; wires that end beside it: and_1_out, CLK, Clear_Pipeline, branchhandlerv2_1_p4, branchhandlerv2_1_p5
  Multiplexer #(.width(5)) multiplexer_6 (
    .in0(multiplexer_5_out), .in1({5{1'b1}}), .out(multiplexer_6_out), .sel(controlunit_1_p6));
  not not_4 (not_4_out, CLK);
  Comparator #(.width(32)) comparator_1 (
    .a(forwarding_unit_1_p12), .b(multiplexer_10_out), .eq(comparator_1_eq));  // open: gt, lt
  and and_2 (and_2_out, controlunit_1_p9, xor_1_out);
  Shifter #(.width(32)) shifter_1 (.in(immediatecomplement_1_p3), .\dist (5'b00010), .out(shifter_1_out));
  // LW_Hazard_Handler lw_hazard_handler_1: pin names not known; wires that end beside it: CLK, lw_hazard_handler_1_p2, lw_hazard_handler_1_p3, lw_hazard_handler_1_p4, lw_hazard_handler_1_p5, lw_hazard_handler_1_p6
  xor xor_1 (xor_1_out, comparator_1_eq, controlunit_1_p8);
  Multiplexer #(.width(32)) multiplexer_7 (
    .in0(TPCPlus4EX), .in1(adder_3_out), .out(multiplexer_7_out), .sel(and_2_out));
  Adder #(.width(32)) adder_3 (.a(TPCPlus4EX), .b(shifter_1_out), .out(adder_3_out));  // open: cin, cout
  // RegisterFile registerfile_1: pin names not known; wires that end beside it: registerfile_1_p1, registerfile_1_p2
  Multiplexer #(.width(32)) multiplexer_8 (
    .in0(multiplexer_7_out), .in1(jtb_1_p6), .out(multiplexer_8_out), .sel(controlunit_1_p10));
  Multiplexer #(.width(32)) multiplexer_9 (
    .in0(multiplexer_8_out), .in1(multiplexer_10_out), .out(multiplexer_9_out), .sel(controlunit_1_p11));
  or or_3 (branchhandlerv2_1_p4, and_2_out, controlunit_1_p11, controlunit_1_p10);
  // Forwarding_Unit forwarding_unit_1: pin names not known; wires that end beside it: controlunit_1_p4, controlunit_1_p3, decoder_alt_1_p9, decoder_alt_1_p10, forwarding_unit_1_p5, forwarding_unit_1_p6, forwarding_unit_1_p7, forwarding_unit_1_p8, forwarding_unit_1_p9, forwarding_unit_1_p10, lw_hazard_handler_1_p3, forwarding_unit_1_p12, immediatecomplement_1_p3, bit_extender_1_out, multiplexer_6_out, TPCPlus4EX, forwarding_unit_1_p17, forwarding_unit_1_p18, forwarding_unit_1_p6, forwarding_unit_1_p20
  Multiplexer #(.select(2), .width(32)) multiplexer_10 (
    .in0(registerfile_1_p1), .in1(ula_1_p4), .in2(multiplexer_15_out), .out(multiplexer_10_out),
    .sel(forwarding_unit_1_p9));  // open: in3
  Multiplexer #(.select(2), .width(32)) multiplexer_11 (
    .in0(registerfile_1_p2), .in1(ula_1_p4), .in2(multiplexer_15_out), .out(forwarding_unit_1_p12),
    .sel(forwarding_unit_1_p10));  // open: in3
  // ID_EXv2 id_exv2_1: pin names not known; wires that end beside it: controlunit_1_p5, controlunit_1_p6, controlunit_1_p7, controlunit_1_p12, controlunit_1_p13, controlunit_1_p14, controlunit_1_p15, controlunit_1_p16, CLK, forwarding_unit_1_p8, id_exv2_1_p11, id_exv2_1_p12, id_exv2_1_p13, lw_hazard_handler_1_p2, id_exv2_1_p15, id_exv2_1_p16, id_exv2_1_p17
  or or_4 (or_4_out, lw_hazard_handler_1_p6, Clear_Pipeline);
  Multiplexer #(.width(32)) multiplexer_12 (
    .in0(ula_1_p6), .in1(forwarding_unit_1_p17), .out(multiplexer_12_out), .sel(id_exv2_1_p17));
  Multiplexer #(.width(32)) multiplexer_13 (
    .in0(undriven), .in1(ula_1_p6), .out(multiplexer_13_out), .sel(id_exv2_1_p16));
  Multiplexer #(.width(32)) multiplexer_14 (
    .in0(multiplexer_12_out), .in1(forwarding_unit_1_p18), .out(multiplexer_14_out), .sel(id_exv2_1_p16));
  // ULA ula_1: pin names not known; wires that end beside it: multiplexer_13_out, multiplexer_14_out, id_exv2_1_p15, ula_1_p4, ula_1_p4, ula_1_p6, forwarding_unit_1_p6, forwarding_unit_1_p20, ula_1_p9, ula_1_p10, forwarding_unit_1_p5, ula_1_p12
  // EX_MEMv2 ex_memv2_1: pin names not known; wires that end beside it: forwarding_unit_1_p8, id_exv2_1_p11, id_exv2_1_p12, id_exv2_1_p13, lw_hazard_handler_1_p2, CLK, forwarding_unit_1_p7, ex_memv2_1_p8, ex_memv2_1_p9, ex_memv2_1_p10, ex_memv2_1_p11
  RAM #(.addrWidth(10), .asyncread("true"), .clearpin("true"), .dataWidth(32)) ram_1 (
    .addr(ula_1_p9[11:2]), .we(ex_memv2_1_p10), .oe(ex_memv2_1_p11), .clk(CLK), .din(ula_1_p10),
    .dout(ram_1_dout), .clr(Clear_Memory));
  Multiplexer #(.width(32)) multiplexer_15 (
    .in0(ula_1_p9), .in1(ram_1_dout), .out(multiplexer_15_out), .sel(ex_memv2_1_p9));
  // MEM_WB mem_wb_1: pin names not known; wires that end beside it: forwarding_unit_1_p7, ex_memv2_1_p8, ex_memv2_1_p9, ula_1_p9, CLK, mem_wb_1_p6, mem_wb_1_p7, mem_wb_1_p8, mem_wb_1_p9
  Multiplexer #(.width(32)) multiplexer_16 (
    .in0(mem_wb_1_p9), .in1(undriven_2), .out(multiplexer_16_out), .sel(mem_wb_1_p8));
  Multiplexer #(.width(32)) multiplexer_17 (
    .in0(multiplexer_16_out), .in1(undriven_3), .out(multiplexer_17_out), .sel(mem_wb_1_p7));

  // Other names for the same wires on the sheet: Clear_t = Clear_Pipeline

  // Notes on the sheet:
  //   Clear PC
  //   contents of rom_1 (hex, n*v repeats v):
  //   20080000 2009000a 200a0000 214b0001 ad0b0000 21080004 214a0001 1549fffb 20080000 200a0000 20100000
  //   11490005 8d0b0000 20b8020 21080004 214a0001 800000b ac100028 8c0c0028 8000013
endmodule

module jtbteste (
  input  update,
  input  clear,
  input  clk,
  input  [31:0] pcIn,
  input  [31:0] instruction,
  input  [31:0] newpc,
  input  [31:0] targuet,
  output [31:0] instructionOut,
  output hit,
  output needUpdate
);

  wire and_1_out, and_3_out, comparator_1_eq, comparator_2_eq, d_ff_1_q, demultiplexer_1_out0,
       demultiplexer_1_out1, demultiplexer_1_out2, demultiplexer_1_out3, demultiplexer_1_out4,
       demultiplexer_1_out5, demultiplexer_1_out6, demultiplexer_1_out7, demultiplexer_2_out0,
       demultiplexer_2_out1, demultiplexer_2_out2, demultiplexer_2_out3, demultiplexer_2_out4,
       demultiplexer_2_out5, demultiplexer_2_out6, demultiplexer_2_out7, not_1_out, not_2_out, not_3_out,
       not_4_out, not_5_out, not_6_out, not_7_out;
  wire [31:0] multiplexer_1_out, register_1_q, register_2_q, register_3_q, register_4_q, register_5_q,
       register_6_q, register_7_q, register_8_q, register_9_q, register_10_q, register_11_q, register_12_q,
       register_13_q, register_14_q, register_15_q, register_16_q;

  Register #(.width(32)) register_1 (.D(newpc), .en(demultiplexer_1_out0), .clk(clk), .Q(register_1_q), .clr(clear));
  Register #(.width(32)) register_2 (.D(targuet), .en(demultiplexer_2_out0), .clk(clk), .Q(register_2_q), .clr(clear));
  Register #(.width(32)) register_3 (.D(newpc), .en(demultiplexer_1_out1), .clk(clk), .Q(register_3_q), .clr(clear));
  Register #(.width(32)) register_4 (.D(targuet), .en(demultiplexer_2_out1), .clk(clk), .Q(register_4_q), .clr(clear));
  Register #(.width(32)) register_5 (.D(newpc), .en(demultiplexer_1_out2), .clk(clk), .Q(register_5_q), .clr(clear));
  Register #(.width(32)) register_6 (.D(targuet), .en(demultiplexer_2_out2), .clk(clk), .Q(register_6_q), .clr(clear));
  not not_1 (not_1_out, instruction[26]);
  not not_2 (not_2_out, instruction[28]);
  and and_1 (and_1_out, not_1_out, instruction[27], not_2_out, not_3_out, not_4_out, not_5_out);
  not not_3 (not_3_out, instruction[29]);
  not not_4 (not_4_out, instruction[30]);
  not not_5 (not_5_out, instruction[31]);
  Register #(.width(32)) register_7 (.D(newpc), .en(demultiplexer_1_out3), .clk(clk), .Q(register_7_q), .clr(clear));
  Multiplexer #(.select(3), .width(32)) multiplexer_1 (
    .in0(register_1_q), .in1(register_3_q), .in2(register_5_q), .in3(register_7_q), .in4(register_9_q),
    .in5(register_11_q), .in6(register_13_q), .in7(register_15_q), .out(multiplexer_1_out), .sel(pcIn[4:2]));
  Register #(.width(32)) register_8 (.D(targuet), .en(demultiplexer_2_out3), .clk(clk), .Q(register_8_q), .clr(clear));
  Multiplexer #(.select(3), .width(32)) multiplexer_2 (
    .in0(register_2_q), .in1(register_4_q), .in2(register_6_q), .in3(register_8_q), .in4(register_10_q),
    .in5(register_12_q), .in6(register_14_q), .in7(register_16_q), .out(instructionOut), .sel(pcIn[4:2]));
  Register #(.width(32)) register_9 (.D(newpc), .en(demultiplexer_1_out4), .clk(clk), .Q(register_9_q), .clr(clear));
  Comparator #(.width(32)) comparator_1 (.a({32{1'b0}}), .b(multiplexer_1_out), .eq(comparator_1_eq));  // open: gt, lt
  Comparator #(.width(32)) comparator_2 (.a(multiplexer_1_out), .b(pcIn), .eq(comparator_2_eq));  // open: gt, lt
  Register #(.width(32)) register_10 (
    .D(targuet), .en(demultiplexer_2_out4), .clk(clk), .Q(register_10_q), .clr(clear));
  Register #(.width(32)) register_11 (.D(newpc), .en(demultiplexer_1_out5), .clk(clk), .Q(register_11_q), .clr(clear));
  not not_6 (not_6_out, comparator_1_eq);
  Register #(.width(32)) register_12 (
    .D(targuet), .en(demultiplexer_2_out5), .clk(clk), .Q(register_12_q), .clr(clear));
  and and_2 (hit, not_6_out, comparator_2_eq);
  Register #(.width(32)) register_13 (.D(newpc), .en(demultiplexer_1_out6), .clk(clk), .Q(register_13_q), .clr(clear));
  Register #(.width(32)) register_14 (
    .D(targuet), .en(demultiplexer_2_out6), .clk(clk), .Q(register_14_q), .clr(clear));
  Register #(.width(32)) register_15 (.D(newpc), .en(demultiplexer_1_out7), .clk(clk), .Q(register_15_q), .clr(clear));
  Register #(.width(32)) register_16 (
    .D(targuet), .en(demultiplexer_2_out7), .clk(clk), .Q(register_16_q), .clr(clear));
  Demultiplexer #(.enable("true"), .select(3)) demultiplexer_1 (
    .out0(demultiplexer_1_out0), .out1(demultiplexer_1_out1), .out2(demultiplexer_1_out2),
    .out3(demultiplexer_1_out3), .out4(demultiplexer_1_out4), .out5(demultiplexer_1_out5),
    .out6(demultiplexer_1_out6), .out7(demultiplexer_1_out7), .in(1'b1), .sel(newpc[4:2]), .en(update));
  Demultiplexer #(.enable("true"), .select(3)) demultiplexer_2 (
    .out0(demultiplexer_2_out0), .out1(demultiplexer_2_out1), .out2(demultiplexer_2_out2),
    .out3(demultiplexer_2_out3), .out4(demultiplexer_2_out4), .out5(demultiplexer_2_out5),
    .out6(demultiplexer_2_out6), .out7(demultiplexer_2_out7), .in(1'b1), .sel(newpc[4:2]), .en(update));
  // Probe on instructionOut
  not not_7 (not_7_out, hit);
  and and_3 (and_3_out, not_7_out, and_1_out);
  D_Flip_Flop d_ff_1 (.D(and_3_out), .clk(clk), .Q(d_ff_1_q));  // open: Qn, preset, reset
  and and_4 (needUpdate, and_3_out, ~d_ff_1_q);  // AND_Gate
endmodule

module IF_ID2 (
  input  clk_IF_ID,
  input  clr_IF_ID,
  input  [31:0] Instruction_IF,
  input  [31:0] PCPlus4_IF,
  input  updateJTB_IF,
  input  enable_IF_ID,
  output [31:0] Instruction_ID,
  output [31:0] PCPus4_ID,
  output updateJTB_ID
);

  Register #(.width(32)) reg_Instruction_IF_ID (
    .D(Instruction_IF), .en(enable_IF_ID), .clk(clk_IF_ID), .Q(Instruction_ID), .clr(clr_IF_ID));
  Register #(.width(32)) reg_PCPlus4_IF_ID (
    .D(PCPlus4_IF), .en(enable_IF_ID), .clk(clk_IF_ID), .Q(PCPus4_ID), .clr(clr_IF_ID));
  Register #(.width(1)) register_1 (
    .D(updateJTB_IF), .en(enable_IF_ID), .clk(clk_IF_ID), .Q(updateJTB_ID), .clr(clr_IF_ID));
endmodule

module jtbteste2 (
  input  update,
  input  clear,
  input  clk,
  input  [31:0] pcIn,
  input  [31:0] instruction,
  input  [31:0] newpc,
  input  [31:0] targuet,
  output [31:0] instructionOut,
  output hit,
  output needUpdate
);

  wire and_1_out, and_3_out, comparator_1_eq, comparator_2_eq, d_ff_1_q, demultiplexer_1_out0,
       demultiplexer_1_out1, demultiplexer_1_out2, demultiplexer_1_out3, demultiplexer_1_out4,
       demultiplexer_1_out5, demultiplexer_1_out6, demultiplexer_1_out7, demultiplexer_2_out0,
       demultiplexer_2_out1, demultiplexer_2_out2, demultiplexer_2_out3, demultiplexer_2_out4,
       demultiplexer_2_out5, demultiplexer_2_out6, demultiplexer_2_out7, not_1_out, not_2_out, not_3_out,
       not_4_out, not_5_out, not_6_out, not_7_out;
  wire [31:0] multiplexer_1_out, register_1_q, register_2_q, register_3_q, register_4_q, register_5_q,
       register_6_q, register_7_q, register_8_q, register_9_q, register_10_q, register_11_q, register_12_q,
       register_13_q, register_14_q, register_15_q, register_16_q;

  Register #(.width(32)) register_1 (.D(newpc), .en(demultiplexer_1_out0), .clk(clk), .Q(register_1_q), .clr(clear));
  Register #(.width(32)) register_2 (.D(targuet), .en(demultiplexer_2_out0), .clk(clk), .Q(register_2_q), .clr(clear));
  Register #(.width(32)) register_3 (.D(newpc), .en(demultiplexer_1_out1), .clk(clk), .Q(register_3_q), .clr(clear));
  Register #(.width(32)) register_4 (.D(targuet), .en(demultiplexer_2_out1), .clk(clk), .Q(register_4_q), .clr(clear));
  Register #(.width(32)) register_5 (.D(newpc), .en(demultiplexer_1_out2), .clk(clk), .Q(register_5_q), .clr(clear));
  Register #(.width(32)) register_6 (.D(targuet), .en(demultiplexer_2_out2), .clk(clk), .Q(register_6_q), .clr(clear));
  not not_1 (not_1_out, instruction[26]);
  not not_2 (not_2_out, instruction[28]);
  and and_1 (and_1_out, not_1_out, instruction[27], not_2_out, not_3_out, not_4_out, not_5_out);
  not not_3 (not_3_out, instruction[29]);
  not not_4 (not_4_out, instruction[30]);
  not not_5 (not_5_out, instruction[31]);
  Register #(.width(32)) register_7 (.D(newpc), .en(demultiplexer_1_out3), .clk(clk), .Q(register_7_q), .clr(clear));
  Multiplexer #(.select(3), .width(32)) multiplexer_1 (
    .in0(register_1_q), .in1(register_3_q), .in2(register_5_q), .in3(register_7_q), .in4(register_9_q),
    .in5(register_11_q), .in6(register_13_q), .in7(register_15_q), .out(multiplexer_1_out), .sel(pcIn[4:2]));
  Register #(.width(32)) register_8 (.D(targuet), .en(demultiplexer_2_out3), .clk(clk), .Q(register_8_q), .clr(clear));
  Multiplexer #(.select(3), .width(32)) multiplexer_2 (
    .in0(register_2_q), .in1(register_4_q), .in2(register_6_q), .in3(register_8_q), .in4(register_10_q),
    .in5(register_12_q), .in6(register_14_q), .in7(register_16_q), .out(instructionOut), .sel(pcIn[4:2]));
  Register #(.width(32)) register_9 (.D(newpc), .en(demultiplexer_1_out4), .clk(clk), .Q(register_9_q), .clr(clear));
  Comparator #(.width(32)) comparator_1 (.a({32{1'b0}}), .b(multiplexer_1_out), .eq(comparator_1_eq));  // open: gt, lt
  Comparator #(.width(32)) comparator_2 (.a(multiplexer_1_out), .b(pcIn), .eq(comparator_2_eq));  // open: gt, lt
  Register #(.width(32)) register_10 (
    .D(targuet), .en(demultiplexer_2_out4), .clk(clk), .Q(register_10_q), .clr(clear));
  Register #(.width(32)) register_11 (.D(newpc), .en(demultiplexer_1_out5), .clk(clk), .Q(register_11_q), .clr(clear));
  not not_6 (not_6_out, comparator_1_eq);
  Register #(.width(32)) register_12 (
    .D(targuet), .en(demultiplexer_2_out5), .clk(clk), .Q(register_12_q), .clr(clear));
  and and_2 (hit, not_6_out, comparator_2_eq);
  Register #(.width(32)) register_13 (.D(newpc), .en(demultiplexer_1_out6), .clk(clk), .Q(register_13_q), .clr(clear));
  Register #(.width(32)) register_14 (
    .D(targuet), .en(demultiplexer_2_out6), .clk(clk), .Q(register_14_q), .clr(clear));
  Register #(.width(32)) register_15 (.D(newpc), .en(demultiplexer_1_out7), .clk(clk), .Q(register_15_q), .clr(clear));
  Register #(.width(32)) register_16 (
    .D(targuet), .en(demultiplexer_2_out7), .clk(clk), .Q(register_16_q), .clr(clear));
  Demultiplexer #(.enable("true"), .select(3)) demultiplexer_1 (
    .out0(demultiplexer_1_out0), .out1(demultiplexer_1_out1), .out2(demultiplexer_1_out2),
    .out3(demultiplexer_1_out3), .out4(demultiplexer_1_out4), .out5(demultiplexer_1_out5),
    .out6(demultiplexer_1_out6), .out7(demultiplexer_1_out7), .in(1'b1), .sel(newpc[4:2]), .en(update));
  Demultiplexer #(.enable("true"), .select(3)) demultiplexer_2 (
    .out0(demultiplexer_2_out0), .out1(demultiplexer_2_out1), .out2(demultiplexer_2_out2),
    .out3(demultiplexer_2_out3), .out4(demultiplexer_2_out4), .out5(demultiplexer_2_out5),
    .out6(demultiplexer_2_out6), .out7(demultiplexer_2_out7), .in(1'b1), .sel(newpc[4:2]), .en(update));
  // Probe on instructionOut
  not not_7 (not_7_out, hit);
  and and_3 (and_3_out, not_7_out, and_1_out);
  D_Flip_Flop d_ff_1 (.D(and_3_out), .clk(clk), .Q(d_ff_1_q));  // open: Qn, preset, reset
  and and_4 (needUpdate, and_3_out, ~d_ff_1_q);  // AND_Gate
endmodule
